// Logisim project LUT_v2.circ as structural Verilog: 5 circuits, main circuit main
module main (
  input  in_1,
  input  in_2,
  input  in_3,
  input  in_4,
  input  in_5,
  input  in_6,
  input  [7:0] in_7,
  input  [7:0] in_8,
  input  [1:0] SC1,
  input  [1:0] SC1_2,
  input  [1:0] SC2,
  input  [1:0] SC2_2,
  input  [1:0] SC3,
  input  [1:0] SC3_2,
  input  in_15,
  input  in_16,
  input  in_17,
  input  in_18,
  input  in_19,
  input  in_20,
  input  [7:0] in_21,
  input  [7:0] in_22,
  input  [1:0] SC1_3,
  input  [1:0] SC1_4,
  input  [1:0] SC2_3,
  input  [1:0] SC2_4,
  input  [1:0] SC3_3,
  input  [1:0] SC3_4,
  output Sum,
  output Carry,
  output out_31,
  output out_32
);

  lut_switch L0 (
    .Config_bits(in_7), .SM1({out_32, Carry, out_31, in_6}), .SM2({out_32, Carry, out_31, in_5}),
    .SM3({out_32, Carry, out_31, in_4}), .SC1(SC1), .SC2(SC2), .SC3(SC3), .Y(Sum));
  lut_switch L2 (
    .Config_bits(in_21), .SM1({out_32, Carry, Sum, in_17}), .SM2({out_32, Carry, Sum, in_16}),
    .SM3({out_32, Carry, Sum, in_15}), .SC1(SC1_3), .SC2(SC2_3), .SC3(SC3_3), .Y(out_31));
  lut_switch L1 (
    .Config_bits(in_8), .SM1({out_32, out_31, Sum, in_3}), .SM2({out_32, out_31, Sum, in_2}),
    .SM3({out_32, out_31, Sum, in_1}), .SC1(SC1_2), .SC2(SC2_2), .SC3(SC3_2), .Y(Carry));
  lut_switch L3 (
    .Config_bits(in_22), .SM1({Carry, out_31, Sum, in_20}), .SM2({Carry, out_31, Sum, in_19}),
    .SM3({Carry, out_31, Sum, in_18}), .SC1(SC1_4), .SC2(SC2_4), .SC3(SC3_4), .Y(out_32));
endmodule

module LUT_v2 (
  input  [7:0] Config_bits,
  input  IP1,
  input  IP2,
  input  IP3,
  output out_5
);

  Multiplexer #(.select(3), .enable("false")) multiplexer_1 (
    .in0(Config_bits[0]), .in1(Config_bits[1]), .in2(Config_bits[2]), .in3(Config_bits[3]),
    .in4(Config_bits[4]), .in5(Config_bits[5]), .in6(Config_bits[6]), .in7(Config_bits[7]), .out(out_5),
    .sel({IP1, IP2, IP3}));
endmodule

module Switch_matrix (
  input  [3:0] SM,
  input  [1:0] SC,
  output out_3
);

  Multiplexer #(.select(2), .enable("false")) multiplexer_1 (
    .in0(SM[0]), .in1(SM[1]), .in2(SM[2]), .in3(SM[3]), .out(out_3), .sel(SC));
endmodule

module lut_switch (
  input  [7:0] Config_bits,
  input  [3:0] SM1,
  input  [3:0] SM2,
  input  [3:0] SM3,
  input  [1:0] SC1,
  input  [1:0] SC2,
  input  [1:0] SC3,
  output Y
);

  wire switch_matrix_1_out_3, switch_matrix_2_out_3, switch_matrix_3_out_3;

  Switch_matrix switch_matrix_1 (.SM(SM1), .SC(SC1), .out_3(switch_matrix_1_out_3));
  Switch_matrix switch_matrix_2 (.SM(SM2), .SC(SC2), .out_3(switch_matrix_2_out_3));
  Switch_matrix switch_matrix_3 (.SM(SM3), .SC(SC3), .out_3(switch_matrix_3_out_3));
  LUT_v2 lut_v2_1 (
    .Config_bits(Config_bits), .IP1(switch_matrix_1_out_3), .IP2(switch_matrix_2_out_3),
    .IP3(switch_matrix_3_out_3), .out_5(Y));
endmodule

module Tristate_matrix (
  input  [2:0] Control,
  input  [2:0] Data,
  output out_3,
  output out_4,
  output out_5
);

  assign out_3 = Control[0] ? Data[0] : 1'bz;  // Controlled_Buffer controlled_buffer_1
  assign out_4 = Control[1] ? Data[1] : 1'bz;  // Controlled_Buffer controlled_buffer_2
  assign out_5 = Control[2] ? Data[2] : 1'bz;  // Controlled_Buffer controlled_buffer_3
endmodule
